// Logisim project Ferrari_Edoardo_892905_arch1lab_progetto.circ as structural Verilog: 8 circuits, main circuit main
module main (
  input  [3:0] in_1,
  input  in_2,
  output overflow
);

  wire clock_out, controlled_buffer_1_out, keyboard_1_avail;
  wire [6:0] cipher_out_4, keyboard_1_data;

  Clock clock (.out(clock_out));
  assign controlled_buffer_1_out = keyboard_1_avail ? clock_out : 1'bz;  // Controlled_Buffer controlled_buffer_1
  Keyboard keyboard_1 (
    .clk(controlled_buffer_1_out), .avail(keyboard_1_avail), .data(keyboard_1_data));  // open: re, clr
  Cesare cipher (.in_2(keyboard_1_data), .in_1(in_1), .out_3(overflow), .out_4(cipher_out_4));
  TTY #(.rows(16), .cols(64)) tty_1 (.data(cipher_out_4), .clk(clock_out), .clr(in_2));  // open: we

  // Other names for the same wires on the sheet: chiave[3:0] = in_1; clear = in_2

  // Notes on the sheet:
  //   schermo
endmodule

module Cesare (
  input  [3:0] in_1,
  input  [6:0] in_2,
  output out_3,
  output [6:0] out_4
);

  wire or_1_out, or_2_out, or_3_out, or_4_out, x____65_a___b_2, x____65_a___b_3, x____90_a___b,
       x____90_a___b_3, x____97_a___b_2, x____97_a___b_3, x____122_a___b, x____122_a___b_3;
  wire [1:0] and_1_out;
  wire [6:0] multiplexer_1_out, sum_cipherchar;

  _7bit_Comparator x____65 (
    .in(in_2), .compare_to(7'b1000001), .A___B_2(x____65_a___b_2), .A___B_3(x____65_a___b_3));  // open: A___B
  _7bit_Comparator x____90 (
    .in(in_2), .compare_to(7'b1011010), .A___B(x____90_a___b), .A___B_3(x____90_a___b_3));  // open: A___B_2
  _7bit_Comparator x____97 (
    .in(in_2), .compare_to(7'b1100001), .A___B_2(x____97_a___b_2), .A___B_3(x____97_a___b_3));  // open: A___B
  _7bit_Comparator x____122 (
    .in(in_2), .compare_to(7'b1111010), .A___B(x____122_a___b), .A___B_3(x____122_a___b_3));  // open: A___B_2
  Cesare_sum sum (.plainchar(in_2), .key(in_1), .overflow(out_3), .cipherchar(sum_cipherchar));
  or or_1 (or_1_out, x____65_a___b_2, x____65_a___b_3);
  or or_2 (or_2_out, x____90_a___b, x____90_a___b_3);
  or or_3 (or_3_out, x____97_a___b_2, x____97_a___b_3);
  or or_4 (or_4_out, x____122_a___b, x____122_a___b_3);
  Multiplexer #(.select(2), .width(7)) multiplexer_1 (
    .in0(in_2), .in1(sum_cipherchar), .in2(sum_cipherchar), .out(multiplexer_1_out), .sel(and_1_out));  // open: in3, en
  and and_1 (and_1_out[0], or_1_out, or_2_out);
  and and_2 (and_1_out[1], or_3_out, or_4_out);
  Cesare_op mod (.in_1(multiplexer_1_out), .in_2(and_1_out[1]), .in_3(and_1_out[0]), .out_4(out_4));

  // Notes on the sheet:
  //   isupper
  //   islower
endmodule

module Cesare_op (
  input  [6:0] in_1,
  input  in_2,
  input  in_3,
  output [6:0] out_4
);

  wire [6:0] adder_1_out, adder_2_out, divider_1_rem, divider_2_rem, subtractor_1_out, subtractor_2_out;

  Subtractor #(.width(7)) subtractor_1 (.a(in_1), .b(7'b1100001), .out(subtractor_1_out));  // open: bin, bout
  Subtractor #(.width(7)) subtractor_2 (.a(in_1), .b(7'b1000001), .out(subtractor_2_out));  // open: bin, bout
  Divider #(.width(7)) divider_1 (.a(subtractor_1_out), .b(7'b0011010), .rem(divider_1_rem));  // open: out, upper
  Divider #(.width(7)) divider_2 (.a(subtractor_2_out), .b(7'b0011010), .rem(divider_2_rem));  // open: out, upper
  Adder #(.width(7)) adder_1 (.a(divider_1_rem), .b(7'b1100001), .out(adder_1_out));  // open: cin, cout
  Adder #(.width(7)) adder_2 (.a(divider_2_rem), .b(7'b1000001), .out(adder_2_out));  // open: cin, cout
  Multiplexer #(.select(2), .width(7)) multiplexer_1 (
    .in0(in_1), .in1(adder_1_out), .in2(adder_2_out), .out(out_4), .sel({in_3, in_2}));  // open: in3, en

  // Other names for the same wires on the sheet: islower = in_2; isupper = in_3

  // Notes on the sheet:
  //   not_char
endmodule

module Cesare_sum (
  input  [3:0] key,
  input  [6:0] plainchar,
  output [6:0] cipherchar,
  output overflow
);

  wire fa_1_remainder_2, fa_2_remainder_2, fa_3_remainder_2, ha_1_remainder, ha_2_remainder, ha_3_remainder;

  HA ha_1 (.input_1(key[0]), .input_2(plainchar[0]), .sum(cipherchar[0]), .remainder(ha_1_remainder));
  FA fa_1 (
    .input_1(key[1]), .input_2(plainchar[1]), .remainder(ha_1_remainder), .sum(cipherchar[1]),
    .remainder_2(fa_1_remainder_2));
  FA fa_2 (
    .input_1(key[2]), .input_2(plainchar[2]), .remainder(fa_1_remainder_2), .sum(cipherchar[2]),
    .remainder_2(fa_2_remainder_2));
  FA fa_3 (
    .input_1(key[3]), .input_2(plainchar[3]), .remainder(fa_2_remainder_2), .sum(cipherchar[3]),
    .remainder_2(fa_3_remainder_2));
  HA ha_2 (.input_1(fa_3_remainder_2), .input_2(plainchar[4]), .sum(cipherchar[4]), .remainder(ha_2_remainder));
  HA ha_3 (.input_1(ha_2_remainder), .input_2(plainchar[5]), .sum(cipherchar[5]), .remainder(ha_3_remainder));
  HA ha_4 (.input_1(ha_3_remainder), .input_2(plainchar[6]), .sum(cipherchar[6]), .remainder(overflow));
endmodule

module _7bit_Comparator (
  input  [6:0] in,
  input  [6:0] compare_to,
  output A___B,
  output A___B_2,
  output A___B_3
);

  wire and_1_out, and_2_out, and_3_out, and_4_out, and_5_out, and_6_out, and_7_out, and_8_out, and_9_out,
       and_10_out, and_11_out, and_12_out, n1bit_comparator_1_out_3, n1bit_comparator_1_out_4,
       n1bit_comparator_1_out_5, n1bit_comparator_2_out_3, n1bit_comparator_2_out_4,
       n1bit_comparator_2_out_5, n1bit_comparator_3_out_3, n1bit_comparator_3_out_4,
       n1bit_comparator_3_out_5, n1bit_comparator_4_out_3, n1bit_comparator_4_out_4,
       n1bit_comparator_4_out_5, n1bit_comparator_5_out_3, n1bit_comparator_5_out_4,
       n1bit_comparator_5_out_5, n1bit_comparator_6_out_3, n1bit_comparator_6_out_4,
       n1bit_comparator_6_out_5, n1bit_comparator_7_out_3, n1bit_comparator_7_out_4, n1bit_comparator_7_out_5;

  _1bit_Comparator u_1bit_comparator_1 (
    .in_1(in[6]), .in_2(compare_to[6]), .out_3(n1bit_comparator_1_out_3), .out_4(n1bit_comparator_1_out_4),
    .out_5(n1bit_comparator_1_out_5));
  _1bit_Comparator u_1bit_comparator_2 (
    .in_1(in[5]), .in_2(compare_to[5]), .out_3(n1bit_comparator_2_out_3), .out_4(n1bit_comparator_2_out_4),
    .out_5(n1bit_comparator_2_out_5));
  _1bit_Comparator u_1bit_comparator_3 (
    .in_1(in[4]), .in_2(compare_to[4]), .out_3(n1bit_comparator_3_out_3), .out_4(n1bit_comparator_3_out_4),
    .out_5(n1bit_comparator_3_out_5));
  _1bit_Comparator u_1bit_comparator_4 (
    .in_1(in[3]), .in_2(compare_to[3]), .out_3(n1bit_comparator_4_out_3), .out_4(n1bit_comparator_4_out_4),
    .out_5(n1bit_comparator_4_out_5));
  _1bit_Comparator u_1bit_comparator_5 (
    .in_1(in[2]), .in_2(compare_to[2]), .out_3(n1bit_comparator_5_out_3), .out_4(n1bit_comparator_5_out_4),
    .out_5(n1bit_comparator_5_out_5));
  _1bit_Comparator u_1bit_comparator_6 (
    .in_1(in[1]), .in_2(compare_to[1]), .out_3(n1bit_comparator_6_out_3), .out_4(n1bit_comparator_6_out_4),
    .out_5(n1bit_comparator_6_out_5));
  _1bit_Comparator u_1bit_comparator_7 (
    .in_1(in[0]), .in_2(compare_to[0]), .out_3(n1bit_comparator_7_out_3), .out_4(n1bit_comparator_7_out_4),
    .out_5(n1bit_comparator_7_out_5));
  and and_1 (and_1_out, n1bit_comparator_1_out_4, n1bit_comparator_2_out_3);
  and and_2 (and_2_out, n1bit_comparator_1_out_4, n1bit_comparator_2_out_5);
  and and_3 (and_3_out, n1bit_comparator_1_out_4, n1bit_comparator_3_out_3, n1bit_comparator_2_out_4);
  and and_4 (and_4_out, n1bit_comparator_1_out_4, n1bit_comparator_3_out_5, n1bit_comparator_2_out_4);
  and and_5 (and_5_out, n1bit_comparator_1_out_4, n1bit_comparator_2_out_4, n1bit_comparator_4_out_3, n1bit_comparator_3_out_4);
  and and_6 (and_6_out, n1bit_comparator_1_out_4, n1bit_comparator_2_out_4, n1bit_comparator_4_out_5, n1bit_comparator_3_out_4);
  and and_7 (and_7_out, n1bit_comparator_1_out_4, n1bit_comparator_2_out_4, n1bit_comparator_3_out_4, n1bit_comparator_5_out_3, n1bit_comparator_4_out_4);
  and and_8 (and_8_out, n1bit_comparator_1_out_4, n1bit_comparator_2_out_4, n1bit_comparator_3_out_4, n1bit_comparator_5_out_5, n1bit_comparator_4_out_4);
  and and_9 (and_9_out, n1bit_comparator_1_out_4, n1bit_comparator_2_out_4, n1bit_comparator_3_out_4, n1bit_comparator_4_out_4, n1bit_comparator_6_out_3, n1bit_comparator_5_out_4);
  and and_10 (and_10_out, n1bit_comparator_1_out_4, n1bit_comparator_2_out_4, n1bit_comparator_6_out_5, n1bit_comparator_3_out_4, n1bit_comparator_4_out_4, n1bit_comparator_5_out_4);
  and and_11 (and_11_out, n1bit_comparator_1_out_4, n1bit_comparator_2_out_4, n1bit_comparator_3_out_4, n1bit_comparator_4_out_4, n1bit_comparator_7_out_3, n1bit_comparator_5_out_4, n1bit_comparator_6_out_4);
  and and_12 (and_12_out, n1bit_comparator_1_out_4, n1bit_comparator_2_out_4, n1bit_comparator_7_out_5, n1bit_comparator_3_out_4, n1bit_comparator_4_out_4, n1bit_comparator_5_out_4, n1bit_comparator_6_out_4);
  or or_1 (A___B, n1bit_comparator_1_out_3, and_1_out, and_3_out, and_5_out, and_7_out, and_9_out, and_11_out);
  or or_2 (A___B_2, n1bit_comparator_1_out_5, and_2_out, and_4_out, and_6_out, and_8_out, and_10_out, and_12_out);
  and and_13 (A___B_3, n1bit_comparator_1_out_4, n1bit_comparator_2_out_4, n1bit_comparator_3_out_4, n1bit_comparator_4_out_4, n1bit_comparator_5_out_4, n1bit_comparator_6_out_4, n1bit_comparator_7_out_4);

  // Notes on the sheet:
  //   A
  //   B
endmodule

module _1bit_Comparator (
  input  in_1,
  input  in_2,
  output out_3,
  output out_4,
  output out_5
);

  and and_1 (out_3, ~in_1, in_2);  // AND_Gate
  and and_2 (out_5, in_1, ~in_2);  // AND_Gate
  nor nor_1 (out_4, out_3, out_5);
endmodule

module FA (
  input  remainder,
  input  input_1,
  input  input_2,
  output sum,
  output remainder_2
);

  wire ha_1_remainder, ha_1_sum, ha_2_remainder;

  HA ha_1 (.input_1(input_1), .input_2(input_2), .sum(ha_1_sum), .remainder(ha_1_remainder));
  HA ha_2 (.input_1(ha_1_sum), .input_2(remainder), .sum(sum), .remainder(ha_2_remainder));
  or or_1 (remainder_2, ha_1_remainder, ha_2_remainder);

  // Notes on the sheet:
  //   semplice full adder
endmodule

module HA (
  input  input_1,
  input  input_2,
  output sum,
  output remainder
);

  xor xor_1 (sum, input_1, input_2);
  and and_1 (remainder, input_1, input_2);

  // Notes on the sheet:
  //   semplice half adder
endmodule
